# Fritzing sketch fritzing-pencil (saved by Fritzing 1.0.1rc)
stripboards: 1

parts:
  Infrared_LED = smd LED [color="Red (633nm)" package="0603 [SMD]"]
  U1 = LIPO-2000mAh [package=lipo-2000]
  R2 = Resistor [tolerance=±5% resistance=220 package="2512 [SMD]"]

nets:
  N1: Infrared_LED.cathode, U1.-
  N2: Infrared_LED.anode, R2.Pin_1
  N3: U1.+, R2.Pin_0
