# Fritzing sketch 20231211-fritzing-exercise (saved by Fritzing 1.0.1rc)
stripboards: 1

parts:
  Composant1 = Arduino Uno (Rev3)
  R1 = Resistor [tolerance=±5% resistance=220 package="1206 [SMD]"]
  LED1 = smd LED [color="Red (633nm)" package="0805 [SMD]"]

nets:
  N1: Composant1.D13/SCK, R1.Pin_0
  N2: Composant1.GND, LED1.cathode
  N3: R1.Pin_1, LED1.anode
